// Digital circuit MainProcessor.dig as structural Verilog
module MainProcessor (
  input  [15:0] IN,
  input  clk,
  output [15:0] OUT
);

  wire ALUOp, ALUsrc, button_1_out, clk_t, DataSRC, dipswitch_1_out, MEM0, nclk, OUTen, PCsrc, PCsub,
       WriteData, writePTR;
  wire [2:0] OPcode;
  wire [12:0] ProgMem_d;
  wire [15:0] addsub_1_p4, addsub_2_p4, bitextender_1_p2, multiplexer_1_out, multiplexer_3_out,
       multiplexer_4_out, PC_q, PTR_q, ramdualport_1_d;

  Register #(.Bits(16), .isProgramCounter("true")) PC (.D(addsub_1_p4), .C(clk_t), .en(1'b1), .Q(PC_q));
  Multiplexer #(.Bits(16)) multiplexer_1 (.sel(PCsrc), .in_0(16'h1), .in_1(bitextender_1_p2), .out(multiplexer_1_out));
  // addsub addsub_1: pin names not known; wires that end beside it: PC_q, multiplexer_1_out, PCsub, addsub_1_p4
  ROM #(.AddrBits(16), .Bits(16)) ProgMem (.A(PC_q), .sel(1'b1), .D({OPcode, ProgMem_d}));
  Register #(.Bits(16)) PTR (.D(addsub_2_p4), .C(clk_t), .en(writePTR), .Q(PTR_q));
  // bitExtender bitextender_1: pin names not known; wires that end beside it: ProgMem_d, bitextender_1_p2
  ControlLogic controllogic_1 (
    .OP(OPcode), .MEM0(MEM0), .PCsrc(PCsrc), .PCsub(PCsub), .DataSRC(DataSRC), .OUTen(OUTen),
    .WritePTR(writePTR), .WriteData(WriteData), .ALUsrc(ALUsrc), .ALUOp(ALUOp));
  Button button_1 (.out(button_1_out));
  Multiplexer multiplexer_2 (.sel(dipswitch_1_out), .in_0(button_1_out), .in_1(clk), .out(clk_t));
  DipSwitch dipswitch_1 (.out(dipswitch_1_out));
  not not_1 (nclk, clk_t);
  Multiplexer #(.Bits(16)) multiplexer_3 (.sel(ALUsrc), .in_0(PTR_q), .in_1(ramdualport_1_d), .out(multiplexer_3_out));
  // addsub addsub_2: pin names not known; wires that end beside it: multiplexer_3_out, bitextender_1_p2, ALUOp, addsub_2_p4
  Multiplexer #(.Bits(16)) multiplexer_4 (.sel(DataSRC), .in_0(addsub_2_p4), .in_1(IN), .out(multiplexer_4_out));
  RAMDualPort #(.AddrBits(16), .Bits(16)) ramdualport_1 (
    .A(PTR_q), .Din(multiplexer_4_out), .str(WriteData), .C(clk_t), .ld(1'b1), .D(ramdualport_1_d));
  Comparator #(.Bits(16)) comparator_1 (.a(ramdualport_1_d), .b({16{1'b0}}), .eq(MEM0));  // open: gt, lt
  Register #(.Bits(16)) OUTreg (.D(ramdualport_1_d), .C(clk_t), .en(OUTen), .Q(OUT));
  Terminal terminal_1 (.D(ramdualport_1_d), .C(clk_t), .en(OUTen));

  // Other names for the same wires on the sheet: sys_clk = clk

  // Notes on the sheet:
  //   clk: Hz: 100
  //   FetchStage
  //   contents of ProgMem (hex, n*v repeats v):
  //   400a,c00e,6001,1,4003,1,4007,1,400a,1,400b,1,400c,2005,e00d,2
  //   ,4003,8000,2001,4002,8000,3,4002,8000,2001,4005,8000,1,4004,8000
  //   ,1,4001,8000,2004,8000,3,8000,2001,6001,8000,6003,8000,2002,8000
  //   ,2,4001,8000,1,6005,8000,8000,6003,8000,2003,4001
  //   DecodeStage
  //   ExecuteStage
  //   MemoryStage
endmodule
